# Fritzing sketch arduino (saved by Fritzing 0.8.5b)

parts:
  Componente1 = Arduino Uno (Rev3) - ICSP
  NRF24L1 = NRF24L01
  C1 = Ceramic Capacitor [capacitance=100nF package="100 mil [THT, multilayer]"]

nets:
  N1: Componente1.D9_PWM, NRF24L1.CE
  N2: Componente1.D10_PWM/SS, NRF24L1.CSN
  N3: Componente1.D11_PWM/MOSI, NRF24L1.MOSI
  N4: Componente1.D12/MISO, NRF24L1.MISO
  N5: Componente1.D13/SCK, NRF24L1.SCK
  3V3: Componente1.3V3, NRF24L1.VCC, C1.1
  GND: Componente1.GND, NRF24L1.GND, C1.0

custom parts:
  NRF24L01: NRF24L01 module
